// Logisim project IT012_Lab01_25521632.circ as structural Verilog: 5 circuits, main circuit TN1
module TN1 (
  input  A,
  input  B,
  input  C,
  output NOT,
  output AND,
  output OR,
  output NAND,
  output NOR,
  output XOR,
  output XNOR,
  output XOR3,
  output CHAIN,
  output NAND3
);

  wire nand_1_out;

  nand nand_1 (nand_1_out, A, B);
  not not_1 (NOT, A);
  and and_1 (AND, A, B);
  or or_1 (OR, A, B);
  xor xor_1 (XOR, A, B);
  ExactlyOne xor_2 (.out(XOR3), .in0(A), .in1(B), .in2(C));
  nand nand_2 (CHAIN, nand_1_out, C);
  nand nand_3 (NAND3, A, B, C);
  nand nand_4 (NAND, A, B);
  nor nor_1 (NOR, A, B);
  xnor xnor_1 (XNOR, A, B);
endmodule

module TN2 (
  input  x,
  input  y,
  input  z,
  output EQ1,
  output EQ2,
  output EQ3,
  output EQ4,
  output EQ5
);

  wire not_1_out, not_2_out, x___x_prime_y_out, x___y_out, x___yz_out, x___z_out, x_prime_y_out,
       x_prime_y_prime_out, x_y__prime_out, x_y__x_z_out, xy__prime_out, yz_out;

  not not_1 (not_1_out, x);
  not not_2 (not_2_out, y);
  or x___y (x___y_out, x, y);
  or x___z (x___z_out, x, z);
  and x_prime_y (x_prime_y_out, not_1_out, y);
  nor x_y__prime (x_y__prime_out, x, y);
  and x_prime_y_prime (x_prime_y_prime_out, not_1_out, not_2_out);
  nand xy__prime (xy__prime_out, x, y);
  and yz (yz_out, y, z);
  and x_y__x_z (x_y__x_z_out, x___y_out, x___z_out);
  or x___x_prime_y (x___x_prime_y_out, x_prime_y_out, x);
  xnor xnor_1 (EQ1, x_y__prime_out, x_prime_y_prime_out);
  xnor xnor_2 (EQ2, x_prime_y_prime_out, xy__prime_out);
  or x___yz (x___yz_out, yz_out, x);
  xnor xnor_3 (EQ4, x___x_prime_y_out, x);
  xnor xnor_4 (EQ5, x___x_prime_y_out, x___y_out);
  xnor xnor_5 (EQ3, x___yz_out, x_y__x_z_out);
endmodule

module TN3 (
  input  A,
  input  B,
  input  C,
  input  D,
  output F
);

  wire A_prime_B_prime_CD_out, A_prime_B_prime_CD_prime_out, A_prime_BC_prime_D_out, A_prime_BCD_out,
       AB_prime_CD_out, ABC_prime_D_out, not_1_out, not_2_out, not_3_out, not_4_out;

  not not_1 (not_1_out, A);
  not not_2 (not_2_out, B);
  not not_3 (not_3_out, C);
  not not_4 (not_4_out, D);
  and A_prime_B_prime_CD_prime (A_prime_B_prime_CD_prime_out, not_1_out, not_2_out, C, not_4_out);
  and A_prime_B_prime_CD (A_prime_B_prime_CD_out, not_1_out, not_2_out, C, D);
  and A_prime_BC_prime_D (A_prime_BC_prime_D_out, not_1_out, B, not_3_out, D);
  and A_prime_BCD (A_prime_BCD_out, not_1_out, B, C, D);
  and AB_prime_CD (AB_prime_CD_out, A, not_2_out, C, D);
  and ABC_prime_D (ABC_prime_D_out, A, B, not_3_out, D);
  or or_1 (F, A_prime_B_prime_CD_prime_out, A_prime_B_prime_CD_out, A_prime_BC_prime_D_out, A_prime_BCD_out, AB_prime_CD_out, ABC_prime_D_out);
endmodule

module TN4 (
  input  A,
  input  B,
  input  C,
  input  D,
  output F_can,
  output F_sop,
  output F_pos
);

  wire A_prime___B_prime___C_prime_out, A_prime___D_out, A_prime_B_prime_C_out, A_prime_B_prime_CD_out,
       A_prime_B_prime_CD_prime_out, A_prime_BC_prime_D_out, A_prime_BCD_out, A_prime_CD_out,
       AB_prime_CD_out, ABC_prime_D_out, B___C_out, B_prime___D_out, B_prime_CD_out, BC_prime_D_out,
       not_1_out, not_2_out, not_3_out, not_4_out;

  not not_1 (not_1_out, A);
  not not_2 (not_2_out, B);
  not not_3 (not_3_out, D);
  not not_4 (not_4_out, C);
  and A_prime_B_prime_C (A_prime_B_prime_C_out, not_1_out, not_2_out, C);
  and B_prime_CD (B_prime_CD_out, not_2_out, C, D);
  and BC_prime_D (BC_prime_D_out, B, not_4_out, D);
  and A_prime_CD (A_prime_CD_out, not_1_out, C, D);
  or B___C (B___C_out, B, C);
  or B_prime___D (B_prime___D_out, not_2_out, D);
  or A_prime___D (A_prime___D_out, not_1_out, D);
  or A_prime___B_prime___C_prime (A_prime___B_prime___C_prime_out, not_1_out, not_2_out, not_4_out);
  and A_prime_B_prime_CD_prime (A_prime_B_prime_CD_prime_out, not_1_out, not_2_out, C, not_3_out);
  and A_prime_B_prime_CD (A_prime_B_prime_CD_out, not_1_out, not_2_out, C, D);
  and A_prime_BC_prime_D (A_prime_BC_prime_D_out, not_1_out, B, not_4_out, D);
  and A_prime_BCD (A_prime_BCD_out, not_1_out, B, C, D);
  and AB_prime_CD (AB_prime_CD_out, A, not_2_out, C, D);
  and ABC_prime_D (ABC_prime_D_out, A, B, not_4_out, D);
  or or_1 (F_sop, A_prime_B_prime_C_out, B_prime_CD_out, BC_prime_D_out, A_prime_CD_out);
  and and_1 (F_pos, B___C_out, B_prime___D_out, A_prime___D_out, A_prime___B_prime___C_prime_out);
  or or_2 (F_can, A_prime_B_prime_CD_prime_out, A_prime_B_prime_CD_out, A_prime_BC_prime_D_out, A_prime_BCD_out, AB_prime_CD_out, ABC_prime_D_out);
endmodule

module TN5 (
  input  A,
  input  B,
  input  C,
  output F
);

  wire xor_1_out;

  xor xor_1 (xor_1_out, A, B);
  xor xor_2 (F, xor_1_out, C);
endmodule
